// Logisim project ULA.circ as structural Verilog: 3 circuits, main circuit main
module main (
  input  [31:0] A,
  input  [31:0] B,
  input  [4:0] shamt,
  input  [3:0] Op_ALU,
  output zero,
  output [31:0] S,
  output overflow
);

  wire and_2_out, and_3_out, or_2_out, overflow_1_overflow;

  // AND_Gate and_1 has open pins: in0=A, in1=B, out=open
  // OR_Gate or_1 has open pins: in0=A, in1=B, out=open
  Adder #(.width(32)) adder_1 (.a(A), .b(B));  // open: out, cin, cout
  Shifter #(.width(32)) shifter_1 (.in(A), .\dist (shamt));  // open: out
  Subtractor #(.width(32)) subtractor_1 (.a(A));  // open: b, out, bin, bout
  Shifter #(.width(32), .shift("lr")) shifter_2 (.in(A), .\dist (shamt));  // open: out
  // XOR_Gate xor_1 has open pins: in0=A, in1=B, out=open
  // NOR_Gate nor_1 has open pins: in0=A, in1=B, out=open
  Comparator #(.width(32)) comparator_1 (.a(A), .b(B));  // open: gt, eq, lt
  Multiplexer #(.select(4), .width(32), .enable("false")) multiplexer_1 (
    .out(S), .sel(Op_ALU));  // open: in0, in1, in2, in3, in4, in5, in6, in7, in8, in9, in10, in11, in12, in13, in14, in15
  overflow overflow_1 (.R(S), .Overflow(overflow_1_overflow));  // open: A, B
  and and_2 (and_2_out, ~Op_ALU[1], ~Op_ALU[1], ~Op_ALU[3], ~Op_ALU[0]);  // AND_Gate
  and and_3 (and_3_out, Op_ALU[0], Op_ALU[1], Op_ALU[2], Op_ALU[3]);
  _32b_equals_zero u_32b_equals_zero_1 (.R(S), .out_2(zero));
  or or_2 (or_2_out, and_2_out, and_3_out);
  and and_4 (overflow, overflow_1_overflow, or_2_out);
endmodule

module overflow (
  input  [31:0] A,
  input  [31:0] B,
  input  [31:0] R,
  output Overflow
);

  wire and_1_out, and_2_out, not_1_out, not_2_out, not_3_out;

  not not_1 (not_1_out, A[31]);
  not not_2 (not_2_out, B[31]);
  not not_3 (not_3_out, R[31]);
  and and_1 (and_1_out, not_1_out, not_2_out, R[31]);
  and and_2 (and_2_out, A[31], B[31], not_3_out);
  or or_1 (Overflow, and_1_out, and_2_out);
endmodule

module _32b_equals_zero (
  input  [31:0] R,
  output out_2
);

  and and_1 (out_2, ~R[0], ~R[1], ~R[2], ~R[3], ~R[4], ~R[5], ~R[6], ~R[7], ~R[8], ~R[9], ~R[10], ~R[11], ~R[12], ~R[13], ~R[14], ~R[15], ~R[16], ~R[17], ~R[18], ~R[19], ~R[20], ~R[21], ~R[22], ~R[23], ~R[24], ~R[25], ~R[26], ~R[27], ~R[28], ~R[29], ~R[30], ~R[31]);  // AND_Gate
endmodule
